# Fritzing sketch Can Test Board v1 (saved by Fritzing 0.9.4)
breadboards: 1

parts:
  R1 = 2,2k Resistor [package=THT]
  Beer_Fill_Sensor_1 = Momentary Switch [package=ksa_sealed_tac_switch]
  Beer_Fill_Sensor_2 = Momentary Switch [package=ksa_sealed_tac_switch]
  Part1 = Arduino Uno (Rev3)
  pin_8_Can_Sense/Start_button = Momentary Switch [package=ksa_sealed_tac_switch]
  R14 = Resistor [tolerance=±5% resistance=220 package=THT]
  R15 = 2,2k Resistor [package=THT]
  R16 = 2,2k Resistor [package=THT]
  R17 = 2,2k Resistor [package=THT]
  R18 = 2,2k Resistor [package=THT]
  pin_3_fill_rail_sol = LED - 5mm [color="Yellow (595nm)" package="5 mm [THT]"]
  pin_4_co2_sol = LED - 5mm [color="Yellow (595nm)" package="5 mm [THT]"]
  pin_5_fill_sol_1 = LED - 5mm [color="Yellow (595nm)" package="5 mm [THT]"]
  pin_6_fill_sol_2 = LED - 5mm [color="Yellow (595nm)" package="5 mm [THT]"]
  pin_7_fill_sol_3 = LED - 5mm [color="Yellow (595nm)" package="5 mm [THT]"]
  Pin_2_canpush = LED - 5mm [color="Yellow (595nm)" package="5 mm [THT]"]
  R19 = 2,2k Resistor [package=THT]
  R20 = 2,2k Resistor [package=THT]
  R21 = 2,2k Resistor [package=THT]
  R22 = 2,2k Resistor [package=THT]
  Beer_Fill_Sensor_3 = Momentary Switch [package=ksa_sealed_tac_switch]

nets:
  N1: R1.Pin_0, Part1.GND, R14.Pin_0, R15.Pin_0, R16.Pin_0, R17.Pin_0, R18.Pin_0, R19.Pin_0, R21.Pin_0, R22.Pin_0
  N2: Beer_Fill_Sensor_1.1, Part1.A0
  N3: Beer_Fill_Sensor_1.3, Beer_Fill_Sensor_2.3, Part1.5V, pin_8_Can_Sense/Start_button.2, Beer_Fill_Sensor_3.4
  N4: Beer_Fill_Sensor_2.1, Part1.A1
  N5: Part1.A2, R20.Pin_0, Beer_Fill_Sensor_3.2
  N6: Part1.D8, pin_8_Can_Sense/Start_button.4, R14.Pin_1
  N7: Part1.D2, Pin_2_canpush.anode
  N8: Part1.D3_PWM, pin_3_fill_rail_sol.anode
  N9: Part1.D4, pin_4_co2_sol.anode
  N10: Part1.D5_PWM, pin_5_fill_sol_1.anode
  N11: Part1.D6_PWM, pin_6_fill_sol_2.anode
  N12: Part1.D7, pin_7_fill_sol_3.anode

custom parts:
  2,2k Resistor: A generic resistor (0.25W)
